# Fritzing sketch Anhaenger (saved by Fritzing 0.9.3b)
circuit board: 8cm x 3cm
breadboards: 1

parts:
  U1 = ATmega 328P [package=dip]
  J1 = AVR ISP 6 Pin [package=2x3-ns]
  R2 = Resistor [tolerance=±5% resistance=10k package=THT]
  Q1 = MOSFET-NCHANNEL [package=to220v]
  LED1 = LED - 3mm [color="Red (633nm)" package="3 mm [THT]"]
  LED2 = LED - 3mm [color="Red (633nm)" package="3 mm [THT]"]
  R4 = Resistor [tolerance=±5% resistance=10k package=THT]
  Xtal2 = Crystal [frequency="16 Mhz" package=THT]
  C6 = Ceramic Capacitor [capacitance=22pF package="200 mil [THT, multilayer]"]
  C5 = Ceramic Capacitor [capacitance=22pF package="200 mil [THT, multilayer]"]
  R3 = Resistor [tolerance=±5% resistance=330 package=THT]
  R5 = Resistor [tolerance=±5% resistance=330 package=THT]
  R6 = Resistor [tolerance=±5% resistance=330 package=THT]
  R7 = Resistor [tolerance=±5% resistance=330 package=THT]
  J5 = female pin header, 3 pins [form="♀ (female)"]
  J6 = female pin header, 3 pins [form="♀ (female)"]
  J8 = female pin header, 3 pins [form="♀ (female)"]
  J9 = female pin header, 3 pins [form="♀ (female)"]
  R8 = Resistor [tolerance=±5% resistance=330 package=THT]
  R9 = Resistor [tolerance=±5% resistance=330 package=THT]
  J10 = female pin header, 2 pins [form="♀ (female)"]
  J11 = female pin header, 2 pins [form="♀ (female)"]
  C7 = Tantalum Capacitor [capacitance=0.1mF package="200 mil [THT, tantalum]"]

nets:
  N1: U1.PC6_(PCINT14/^RESET)_[RESET], J1.5, R2.Pin_1
  N2: U1.PD2_(PCINT18/INT0)_[D2], J11.pin1
  N3: U1.PD3_(PCINT19/OC2B/INT1)_[D3_PWM], J10.pin1
  N4: U1.PD4_(PCINT20/XCK/T0)_[D4], R5.Pin_0
  N5: U1.VCC, U1.AVCC, J1.2, R2.Pin_0, J5.pin1
  N6: U1.GND, J1.6, Q1.S, R4.Pin_0, C6.1, C5.0, J10.pin2, J11.pin2
  N7: U1.PB6_(PCINT6/XTAL1/TOSC1)_[XTAL1], Xtal2.pin_1, C5.1
  N8: U1.PB7_(PCINT7/XTAL2/TOSC2)_[XTAL2], Xtal2.pin_0, C6.0
  N9: U1.PD5_(PCINT21/OC0B/T1)_[D5_PWM], R6.Pin_0
  N10: U1.PD6_(PCINT22/OC0A/AIN0)_[D6_PWM], R7.Pin_0
  N11: U1.PB0_(PCINT0/CLK0/ICP1)_[D8], Q1.G, R4.Pin_1
  N12: U1.PB1_(OC1A/PCINT1)_[D9_PWM], R9.Pin_1
  N13: U1.PB2_(^SS/OC1B/PCINT2)_[D10_PWM], R8.Pin_1
  N14: U1.PB3_(MOSI/OC2A/PCINT3)_[D11_PWM], J1.4
  N15: U1.PB4_(MISO/PCINT4)_[D12], J1.1
  N16: U1.PB5_(SCK/PCINT5)_[D13], J1.3, R3.Pin_0
  N17: Q1.D, LED1.cathode, LED2.cathode, J5.pin3, J6.pin1, J8.pin1, J9.pin1, C7.-
  N18: LED1.anode, R3.Pin_1
  N19: LED2.anode, R5.Pin_1
  N20: R6.Pin_1, J6.pin2
  N21: R7.Pin_1, J5.pin2
  N22: J6.pin3, C7.+
  N23: J8.pin2, R8.Pin_0
  N24: J8.pin3, J9.pin3
  N25: J9.pin2, R9.Pin_0

custom parts:
  ATmega 328P: Atmel ATmega 328P-PU Microcontroller
